# Fritzing sketch hw2 (saved by Fritzing 0.9.3b)
breadboards: 1

parts:
  Part1 = Photon
  R1 = Resistor [tolerance=±5% resistance=5.1k package=THT]
  R2 = Basic Flex Resistor

nets:
  N1: Part1.A0, R1.Pin_0, R2.Pin_2
  N2: Part1.GND, R1.Pin_1
  N3: Part1.VIN, R2.pin_1
